# Fritzing sketch Untitled Sketch (saved by Fritzing 1.0.4)
breadboards: 1

parts:
  Adafruit_INA228_I2C_Power_Monitor1 = Adafruit INA228 I2C Power Monitor [part_number=#5832]
  Part1 = Adafruit Feather RP2040 [part_number="Adafruit #4884"]
  R1 = Resistor [tolerance=±5% power=0.25W resistance=4.7k package=THT]
  R2 = Resistor [tolerance=±5% power=0.25W resistance=4.7k package=THT]  # not connected
  R3 = Resistor [tolerance=±5% power=0.25W resistance=4.7k package=THT]  # not connected
  R5 = Resistor [tolerance=±5% power=0.25W resistance=4.7k package=THT]

nets:
  N1: Adafruit_INA228_I2C_Power_Monitor1.SCL, Part1.SCL, R1.Pin_0
  VCC: Adafruit_INA228_I2C_Power_Monitor1.VCC, Part1.+3V3, R1.Pin_1, R5.Pin_1
  GND: Adafruit_INA228_I2C_Power_Monitor1.GND, Part1.GND
  N2: Adafruit_INA228_I2C_Power_Monitor1.SDA, Part1.SDA, R5.Pin_0

custom parts:
  Adafruit INA228 I2C Power Monitor: The INA228 is an amazing power monitoring chip, with best-of-everything support: up to 85VDC common-mode, high or low side measurements, 20-bit (!) ADC for precision measurements from milliamp to Amp, and I2C interface for easy configuration of alerts, oversampling, gain adjustments and more! This breakout board may well be the last current sensing solution you every need to buy. Not only can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
  Adafruit Feather RP2040: A new chip means a new Feather, and the Raspberry Pi RP2040 is no exception. When we saw this chip we thought "this chip is going to be awesome when we give it the Feather Treatment" and so we did! This Feather features the RP2040, and all niceties you know and love about Feather Measures 2.0" x 0.9" x 0.28" (50.8mm x 22.8mm x 7mm) without headers soldered in Light as a (large?) feather - 5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
